# Fritzing sketch practica01 (saved by Fritzing 0.9.2b)
breadboards: 1

parts:
  Parte1 = Arduino Uno (Rev3)
  LED3 = LED - 5mm [color="Green (560nm)" package="5 mm [THT]"]
  R3 = Resistor [tolerance=±5% resistance=220 package=THT]
  R4 = Rotary Potentiometer (Small) [maximum_resistance=100kΩ package=THT]

nets:
  N1: Parte1.A0, R4.wiper
  N2: Parte1.GND, LED3.cathode, R4.leg2
  N3: Parte1.D3_PWM, R3.Pin_0
  N4: Parte1.5V, R4.leg1
  N5: LED3.anode, R3.Pin_1
